# Fritzing sketch arduino_eth (saved by Fritzing 0.9.0b)
breadboards: 1

parts:
  U1 = TEMPERATURE-SENSOR [package=to-92]
  Composant1 = Arduino Board Ethernet
  R1 = Resistor [package="2010 [SMD]"]

nets:
  GND: U1.GND, Composant1.GND
  N1: U1.ADJ, Composant1.D2_PWM, R1.Pin_1
  VCC: U1.VCC, Composant1.5V, R1.Pin_0
