# Fritzing sketch arduino_nano_hc06 (saved by Fritzing 0.9.0b)
breadboards: 1

parts:
  Composant1 = Arduino Nano (Rev3.0)
  Composant2 = Bluetooth HC-06
  RHT1 = Humidity and Temperature Sensor RHT03
  R1 = Resistor [tolerance=±5% resistance=220 package=THT]

nets:
  GND: Composant1.GND, Composant2.GND, RHT1.GND_2
  N1: Composant1.D3, RHT1.Data-signal, R1.Pin_0
  N2: Composant1.D10, Composant2.TXD
  N3: Composant1.D11/MOSI, Composant2.RXD
  VCC: Composant1.5V, Composant2.VCC, RHT1.Vcc, R1.Pin_1
